# Fritzing sketch model (saved by Fritzing 0.9.2b)
breadboards: 1

parts:
  Part1 = Arduino Uno (Rev3)
  LED1 = LED - 5mm [color="Red (633nm)" package="5 mm [THT]"]
  R1 = Resistor [tolerance=±5% resistance=10k package=THT]
  Part2 = SRF05 Ultrasonic Rangefinder

nets:
  N1: Part1.D2, R1.Pin_1
  N2: Part1.D5_PWM, Part2.connector10
  N3: Part1.D6_PWM, Part2.connector9
  N4: Part1.5V, Part2.connector8
  N5: Part1.GND, LED1.cathode, Part2.connector11
  N6: LED1.anode, R1.Pin_0
